# Fritzing sketch 555_test (saved by Fritzing 0.7.7b)
breadboards: 1

parts:
  IC1 = 555 Timer [package="DIP8 [THT]"]
  R6 = Resistor [tolerance=±5% resistance=220k package=THT]
  C1 = Ceramic Capacitor [capacitance=0.47µF package="100 mil [THT, multilayer]"]
  R8 = Resistor [tolerance=±5% resistance=3.3k package=THT]
  R9 = Resistor [tolerance=±5% resistance=150 package=THT]
  LED1 = LED - 5mm [color="Red (633nm)" package="5 mm [THT]"]

nets:
  GND: IC1.Ground, C1.1, LED1.cathode
  N1: IC1.Trigger, IC1.Threshold, R6.Pin_1, C1.0
  N2: IC1.Output, R9.Pin_1
  3V: IC1.Reset, IC1.Vcc_Supply_Voltage, R8.Pin_0
  N3: IC1.Discharge, R6.Pin_0, R8.Pin_1
  N4: R9.Pin_0, LED1.anode
