# Fritzing sketch rinnande ljus protoboard (saved by Fritzing 0.7.7b)
stripboards: 1

parts:
  IC1 = IC, DIP package, 16 pins [chip_label=4016 spacing=300mil]
  U1 = 555 Timer [package="DIP8 [THT]"]
  R2 = Resistor [resistance=220 tolerance=±5% package=THT]
  R3 = Resistor [resistance=3.3k tolerance=±5% package=THT]
  R5 = Trimmer Potentiometer [maximum_resistance=470kΩ package=THT]
  R6 = Resistor [tolerance=±5% resistance=220k package=THT]
  C1 = Ceramic Capacitor [capacitance=0.47µF package="100 mil [THT, multilayer]"]
  LED1 = LED - 5mm [color="Red (633nm)" package="5 mm [THT]"]
  LED2 = LED - 5mm [color="Red (633nm)" package="5 mm [THT]"]
  LED3 = LED - 5mm [color="Red (633nm)" package="5 mm [THT]"]
  LED4 = LED - 5mm [color="Red (633nm)" package="5 mm [THT]"]
  LED5 = LED - 5mm [color="Red (633nm)" package="5 mm [THT]"]
  LED6 = LED - 5mm [color="Red (633nm)" package="5 mm [THT]"]
  LED7 = LED - 5mm [color="Red (633nm)" package="5 mm [THT]"]
  LED8 = LED - 5mm [color="Red (633nm)" package="5 mm [THT]"]
  LED9 = LED - 5mm [color="Red (633nm)" package="5 mm [THT]"]
  LED10 = LED - 5mm [color="Red (633nm)" package="5 mm [THT]"]
  J1 = Screw terminal - 2 pins [package=THT]

nets:
  N1: IC1.pin1, LED6.anode
  N2: IC1.pin2, LED2.anode
  N3: IC1.pin3, LED1.anode
  N4: IC1.pin4, LED3.anode
  N5: IC1.pin5, LED7.anode
  N6: IC1.pin6, LED8.anode
  N7: IC1.pin7, LED4.anode
  GND: IC1.pin8, IC1.pin13, IC1.pin15, U1.Ground, R2.Pin_1, C1.0, J1.pin2
  N8: IC1.pin9, LED9.anode
  N9: IC1.pin10, LED5.anode
  N10: IC1.pin11, LED10.anode
  N11: IC1.pin14, U1.Output
  5V: IC1.pin16, U1.Reset, U1.Vcc_Supply_Voltage, R3.Pin_0, J1.pin1
  N12: U1.Trigger, U1.Threshold, R5.wiper, C1.1
  N13: U1.Discharge, R3.Pin_1, R6.Pin_0
  N14: R2.Pin_0, LED1.cathode, LED2.cathode, LED3.cathode, LED4.cathode, LED5.cathode, LED6.cathode, LED7.cathode, LED8.cathode, LED9.cathode, LED10.cathode
  N15: R5.leg2, R6.Pin_1
