# Fritzing sketch rinnande ljus (saved by Fritzing 0.7.7b)
breadboards: 1

parts:
  U1 = 555 Timer [package="DIP8 [THT]"]
  R5 = Trimmer Potentiometer [maximum_resistance=470kΩ package=THT]
  R6 = Resistor [tolerance=±5% resistance=220k package=THT]
  C1 = Ceramic Capacitor [capacitance=0.47µF package="100 mil [THT, multilayer]"]
  LED1 = LED - 5mm [color="Red (633nm)" package="5 mm [THT]"]
  LED2 = LED - 5mm [color="Red (633nm)" package="5 mm [THT]"]
  LED3 = LED - 5mm [color="Red (633nm)" package="5 mm [THT]"]
  LED4 = LED - 5mm [color="Red (633nm)" package="5 mm [THT]"]
  LED5 = LED - 5mm [color="Red (633nm)" package="5 mm [THT]"]
  LED6 = LED - 5mm [color="Red (633nm)" package="5 mm [THT]"]
  LED7 = LED - 5mm [color="Red (633nm)" package="5 mm [THT]"]
  LED8 = LED - 5mm [color="Red (633nm)" package="5 mm [THT]"]
  LED9 = LED - 5mm [color="Red (633nm)" package="5 mm [THT]"]
  LED10 = LED - 5mm [color="Red (633nm)" package="5 mm [THT]"]
  R7 = Resistor [tolerance=±5% resistance=75 package=THT]
  R8 = Resistor [tolerance=±5% resistance=3.3k package=THT]
  IC1 = IC, DIP package, 16 pins [chip_label=4017]
  VCC1 = Battery

nets:
  GND: U1.Ground, C1.1, R7.Pin_1, IC1.pin8, IC1.pin13, IC1.pin15, VCC1.-
  N1: U1.Trigger, U1.Threshold, R5.wiper, C1.0
  N2: U1.Output, IC1.pin14
  3V: U1.Reset, U1.Vcc_Supply_Voltage, R8.Pin_0, IC1.pin16, VCC1.+
  N3: U1.Discharge, R6.Pin_0, R8.Pin_1
  N4: R5.leg2, R6.Pin_1
  N5: LED1.cathode, LED2.cathode, LED3.cathode, LED4.cathode, LED5.cathode, LED6.cathode, LED7.cathode, LED8.cathode, LED9.cathode, LED10.cathode, R7.Pin_0
  N6: LED1.anode, IC1.pin3
  N7: LED2.anode, IC1.pin2
  N8: LED3.anode, IC1.pin4
  N9: LED4.anode, IC1.pin7
  N10: LED5.anode, IC1.pin10
  N11: LED6.anode, IC1.pin1
  N12: LED7.anode, IC1.pin5
  N13: LED8.anode, IC1.pin6
  N14: LED9.anode, IC1.pin9
  N15: LED10.anode, IC1.pin11
